// Digital circuit half_adder.dig as structural Verilog
module half_adder (
  input  E1,
  input  E2,
  output S,
  output Cout
);

  wire nor_1_out, nor_2_out, nor_3_out, nor_4_out, nor_5_out, nor_7_out;

  nor nor_1 (nor_1_out, E1, E2);
  nor nor_2 (nor_2_out, E1, nor_1_out);
  nor nor_3 (nor_3_out, nor_1_out, E2);
  nor nor_4 (nor_4_out, E1, E1);
  nor nor_5 (nor_5_out, E2, E2);
  nor nor_6 (Cout, nor_4_out, nor_5_out);
  nor nor_7 (nor_7_out, nor_2_out, nor_3_out);
  nor nor_8 (S, nor_7_out, nor_7_out);
endmodule
