// Digital circuit ABCDE.dig as structural Verilog
module ABCDE (
  input  EO,
  input  E0N,
  input  E1,
  input  E1N,
  input  E2N,
  output A,
  output B,
  output C,
  output D,
  output E
);

  and and_1 (A, E0N, E1N);
  and and_2 (B, E0N, E1N, E2N);
  and and_3 (C, E0N, E1);
  and and_4 (D, E0N, E1, E2N);

  assign E = EO;
endmodule
