// Digital circuit MULTIPLICADOR.dig as structural Verilog
module MULTIPLICADOR (
  input  B3,
  input  B2,
  input  B1,
  input  B0,
  input  A4,
  input  A3,
  input  A2,
  input  A1,
  input  A0,
  input  B4,
  input  B5,
  input  A5_2,
  output a9,
  output a8,
  output a7,
  output a6,
  output a5,
  output a4_2,
  output a3_2,
  output a2_2,
  output a1_2,
  output a0_2,
  output a10,
  output a11
);

  // multiplicação multiplicação_1: pin names not known; wires that end beside it: A5_2, a11, A4, a10, A3, a9, A2, a8, A1, a7, A0, a6, B5, a5, B4, a4_2, B3, a3_2, B2, a2_2, B1, a1_2, B0, a0_2
endmodule
