// Digital circuit adder_2.dig as structural Verilog
module adder_2 (
  input  A1,
  input  A2,
  input  A3,
  input  A4,
  input  A5,
  input  A6,
  input  B1,
  input  B2,
  input  B3,
  input  B4,
  input  B5,
  input  B6,
  output S,
  output S1,
  output S2,
  output S3,
  output S4,
  output S5,
  output S6
);

  wire full_adder_1_cout, full_adder_2_cout, full_adder_3_cout, full_adder_4_cout, half_adder_1_cout;

  half_adder half_adder_1 (.E1(A1), .E2(B1), .S(S), .Cout(half_adder_1_cout));
  full_adder full_adder_1 (.E1(A2), .E2(B2), .Cin(half_adder_1_cout), .S(S1), .Cout(full_adder_1_cout));
  full_adder full_adder_2 (.E1(A3), .E2(B3), .Cin(full_adder_1_cout), .S(S2), .Cout(full_adder_2_cout));
  full_adder full_adder_3 (.E1(A4), .E2(B4), .Cin(full_adder_2_cout), .S(S3), .Cout(full_adder_3_cout));
  full_adder full_adder_4 (.E1(A5), .E2(B5), .Cin(full_adder_3_cout), .S(S4), .Cout(full_adder_4_cout));
  full_adder full_adder_5 (.E1(A6), .E2(B6), .Cin(full_adder_4_cout), .S(S5), .Cout(S6));
endmodule
