// Digital circuit full_adder.dig as structural Verilog
module full_adder (
  input  E1,
  input  E2,
  input  Cin,
  output S,
  output Cout
);

  wire nor_1_out, nor_2_out, nor_3_out, nor_4_out, nor_5_out, nor_6_out, nor_7_out, nor_8_out, nor_9_out,
       nor_10_out, nor_11_out, nor_12_out, nor_13_out, nor_14_out, nor_15_out, nor_16_out, nor_17_out,
       nor_18_out, nor_19_out, nor_20_out, nor_22_out;

  nor nor_1 (nor_1_out, E1, E2);
  nor nor_2 (nor_2_out, E2, E2);
  nor nor_3 (nor_3_out, Cin, Cin);
  nor nor_4 (nor_4_out, Cin, Cin);
  nor nor_5 (nor_5_out, E1, E1);
  nor nor_6 (nor_6_out, E1, E1);
  nor nor_7 (nor_7_out, E2, E2);
  nor nor_8 (nor_8_out, E1, nor_1_out);
  nor nor_9 (nor_9_out, nor_1_out, E2);
  nor nor_10 (nor_10_out, nor_2_out, nor_3_out);
  nor nor_11 (nor_11_out, nor_4_out, nor_5_out);
  nor nor_12 (nor_12_out, nor_6_out, nor_7_out);
  nor nor_13 (nor_13_out, nor_8_out, nor_9_out);
  nor nor_14 (nor_14_out, nor_10_out, nor_11_out);
  nor nor_15 (nor_15_out, nor_13_out, nor_13_out);
  nor nor_16 (nor_16_out, nor_14_out, nor_14_out);
  nor nor_17 (nor_17_out, nor_15_out, Cin);
  nor nor_18 (nor_18_out, nor_16_out, nor_12_out);
  nor nor_19 (nor_19_out, nor_15_out, nor_17_out);
  nor nor_20 (nor_20_out, nor_17_out, Cin);
  nor nor_21 (Cout, nor_18_out, nor_18_out);
  nor nor_22 (nor_22_out, nor_19_out, nor_20_out);
  nor nor_23 (S, nor_22_out, nor_22_out);
endmodule
