// Digital circuit multiplicacao.dig as structural Verilog
module multiplicacao (
  input  B1,
  input  B2,
  input  B3,
  input  B4,
  input  B5,
  input  B6,
  input  A1,
  input  A2,
  input  A3,
  input  A4,
  input  A5,
  input  A6,
  output C1,
  output C2,
  output C3,
  output C4,
  output C5,
  output C6,
  output C7,
  output C8,
  output C9,
  output C10,
  output C11,
  output C12
);

  wire adder_1_s1, adder_1_s2, adder_1_s3, adder_1_s4, adder_1_s5, adder_1_s6, adder_2_1_s1, adder_2_1_s2,
       adder_2_1_s3, adder_2_1_s4, adder_2_1_s5, adder_2_1_s6, adder_2_2_s1, adder_2_2_s2, adder_2_2_s3,
       adder_2_2_s4, adder_2_2_s5, adder_2_2_s6, adder_2_3_s1, adder_2_3_s2, adder_2_3_s3, adder_2_3_s4,
       adder_2_3_s5, adder_2_3_s6, produto_1_s2, produto_1_s3, produto_1_s4, produto_1_s5, produto_1_s6,
       produto_2_s1, produto_2_s2, produto_2_s3, produto_2_s4, produto_2_s5, produto_2_s6, produto_3_s1,
       produto_3_s2, produto_3_s3, produto_3_s4, produto_3_s5, produto_3_s6, produto_4_s1, produto_4_s2,
       produto_4_s3, produto_4_s4, produto_4_s5, produto_4_s6, produto_5_s1, produto_5_s2, produto_5_s3,
       produto_5_s4, produto_5_s5, produto_5_s6, produto_6_s1, produto_6_s2, produto_6_s3, produto_6_s4,
       produto_6_s5, produto_6_s6;

  produto produto_1 (
    .B6(B6), .B5(B5), .B4(B4), .B3(B3), .B2(B2), .B1(B1), .A(A1), .S1(C1), .S2(produto_1_s2),
    .S3(produto_1_s3), .S4(produto_1_s4), .S5(produto_1_s5), .S6(produto_1_s6));
  produto produto_2 (
    .B6(B6), .B5(B5), .B4(B4), .B3(B3), .B2(B2), .B1(B1), .A(A2), .S1(produto_2_s1), .S2(produto_2_s2),
    .S3(produto_2_s3), .S4(produto_2_s4), .S5(produto_2_s5), .S6(produto_2_s6));
  produto produto_3 (
    .B6(B6), .B5(B5), .B4(B4), .B3(B3), .B2(B2), .B1(B1), .A(A3), .S1(produto_3_s1), .S2(produto_3_s2),
    .S3(produto_3_s3), .S4(produto_3_s4), .S5(produto_3_s5), .S6(produto_3_s6));
  produto produto_4 (
    .B6(B6), .B5(B5), .B4(B4), .B3(B3), .B2(B2), .B1(B1), .A(A4), .S1(produto_4_s1), .S2(produto_4_s2),
    .S3(produto_4_s3), .S4(produto_4_s4), .S5(produto_4_s5), .S6(produto_4_s6));
  produto produto_5 (
    .B6(B6), .B5(B5), .B4(B4), .B3(B3), .B2(B2), .B1(B1), .A(A5), .S1(produto_5_s1), .S2(produto_5_s2),
    .S3(produto_5_s3), .S4(produto_5_s4), .S5(produto_5_s5), .S6(produto_5_s6));
  produto produto_6 (
    .B6(B6), .B5(B5), .B4(B4), .B3(B3), .B2(B2), .B1(B1), .A(A6), .S1(produto_6_s1), .S2(produto_6_s2),
    .S3(produto_6_s3), .S4(produto_6_s4), .S5(produto_6_s5), .S6(produto_6_s6));
  adder adder_1 (
    .A1(produto_1_s2), .A2(produto_1_s3), .A3(produto_1_s4), .A4(produto_1_s5), .A5(produto_1_s6),
    .B1(produto_2_s1), .B2(produto_2_s2), .B3(produto_2_s3), .B4(produto_2_s4), .B5(produto_2_s5),
    .B6(produto_2_s6), .S(C2), .S1(adder_1_s1), .S2(adder_1_s2), .S3(adder_1_s3), .S4(adder_1_s4),
    .S5(adder_1_s5), .S6(adder_1_s6));
  adder_2 adder_2_1 (
    .A1(adder_1_s1), .A2(adder_1_s2), .A3(adder_1_s3), .A4(adder_1_s4), .A5(adder_1_s5), .A6(adder_1_s6),
    .B1(produto_3_s1), .B2(produto_3_s2), .B3(produto_3_s3), .B4(produto_3_s4), .B5(produto_3_s5),
    .B6(produto_3_s6), .S(C3), .S1(adder_2_1_s1), .S2(adder_2_1_s2), .S3(adder_2_1_s3), .S4(adder_2_1_s4),
    .S5(adder_2_1_s5), .S6(adder_2_1_s6));
  adder_2 adder_2_2 (
    .A1(adder_2_1_s1), .A2(adder_2_1_s2), .A3(adder_2_1_s3), .A4(adder_2_1_s4), .A5(adder_2_1_s5),
    .A6(adder_2_1_s6), .B1(produto_4_s1), .B2(produto_4_s2), .B3(produto_4_s3), .B4(produto_4_s4),
    .B5(produto_4_s5), .B6(produto_4_s6), .S(C4), .S1(adder_2_2_s1), .S2(adder_2_2_s2), .S3(adder_2_2_s3),
    .S4(adder_2_2_s4), .S5(adder_2_2_s5), .S6(adder_2_2_s6));
  adder_2 adder_2_3 (
    .A1(adder_2_2_s1), .A2(adder_2_2_s2), .A3(adder_2_2_s3), .A4(adder_2_2_s4), .A5(adder_2_2_s5),
    .A6(adder_2_2_s6), .B1(produto_5_s1), .B2(produto_5_s2), .B3(produto_5_s3), .B4(produto_5_s4),
    .B5(produto_5_s5), .B6(produto_5_s6), .S(C5), .S1(adder_2_3_s1), .S2(adder_2_3_s2), .S3(adder_2_3_s3),
    .S4(adder_2_3_s4), .S5(adder_2_3_s5), .S6(adder_2_3_s6));
  adder_2 adder_2_4 (
    .A1(adder_2_3_s1), .A2(adder_2_3_s2), .A3(adder_2_3_s3), .A4(adder_2_3_s4), .A5(adder_2_3_s5),
    .A6(adder_2_3_s6), .B1(produto_6_s1), .B2(produto_6_s2), .B3(produto_6_s3), .B4(produto_6_s4),
    .B5(produto_6_s5), .B6(produto_6_s6), .S(C6), .S1(C7), .S2(C8), .S3(C9), .S4(C10), .S5(C11), .S6(C12));
endmodule
