// Digital circuit produto.dig as structural Verilog
module produto (
  input  B6,
  input  B5,
  input  B4,
  input  B3,
  input  B2,
  input  B1,
  input  A,
  output S1,
  output S2,
  output S3,
  output S4,
  output S5,
  output S6
);

  wire nor_1_out, nor_2_out, nor_3_out, nor_4_out, nor_5_out, nor_6_out, nor_7_out, nor_8_out, nor_9_out,
       nor_10_out, nor_11_out, nor_12_out;

  nor nor_1 (nor_1_out, A, A);
  nor nor_2 (nor_2_out, B1, B1);
  nor nor_3 (nor_3_out, A, A);
  nor nor_4 (nor_4_out, B2, B2);
  nor nor_5 (nor_5_out, A, A);
  nor nor_6 (nor_6_out, B3, B3);
  nor nor_7 (nor_7_out, A, A);
  nor nor_8 (nor_8_out, B4, B4);
  nor nor_9 (nor_9_out, A, A);
  nor nor_10 (nor_10_out, B5, B5);
  nor nor_11 (nor_11_out, A, A);
  nor nor_12 (nor_12_out, B6, B6);
  nor nor_13 (S1, nor_1_out, nor_2_out);
  nor nor_14 (S2, nor_3_out, nor_4_out);
  nor nor_15 (S3, nor_5_out, nor_6_out);
  nor nor_16 (S4, nor_7_out, nor_8_out);
  nor nor_17 (S5, nor_9_out, nor_10_out);
  nor nor_18 (S6, nor_11_out, nor_12_out);
endmodule
