// Digital circuit SEMAFORO.dig as structural Verilog
module SEMAFORO (
  input  clk
);

  wire abcde_1_a, abcde_1_b, abcde_1_c, abcde_1_d, abcde_1_e, and_1_out, and_2_out, and_3_out, and_4_out,
       and_5_out, and_6_out, and_7_out, and_8_out, and_9_out, and_10_out, and_11_out, and_12_out,
       button_1_out, E0_nq, E0_q, E1_nq, E1_q, E2_nq, E2_q, not_1_out, or_1_out, or_2_out, rs_ff_as_1_nq,
       rs_ff_as_1_q;

  Button button_1 (.out(button_1_out));
  RS_FF_AS rs_ff_as_1 (.S(button_1_out), .R(abcde_1_e), .Q(rs_ff_as_1_q), .nQ(rs_ff_as_1_nq));
  and and_1 (and_1_out, E2_q, rs_ff_as_1_q, E0_nq);
  and and_2 (and_2_out, E1_q, E2_nq);
  and and_3 (and_3_out, E0_nq, E1_nq, E2_q, rs_ff_as_1_nq);
  and and_4 (and_4_out, E0_q, E2_nq);
  and and_5 (and_5_out, E0_nq, E2_nq);
  and and_6 (and_6_out, E1_q, rs_ff_as_1_q);
  ABCDE abcde_1 (
    .EO(E0_q), .E0N(E0_nq), .E1(E1_q), .E1N(E1_nq), .E2N(E2_nq), .A(abcde_1_a), .B(abcde_1_b), .C(abcde_1_c),
    .D(abcde_1_d), .E(abcde_1_e));
  D_FF E0 (.D(and_1_out), .C(clk), .Q(E0_q), .nQ(E0_nq));
  or or_1 (or_1_out, and_2_out, and_3_out, and_4_out);
  or or_2 (or_2_out, and_5_out, and_6_out);
  D_FF E1 (.D(or_1_out), .C(clk), .Q(E1_q), .nQ(E1_nq));
  D_FF E2 (.D(or_2_out), .C(clk), .Q(E2_q), .nQ(E2_nq));
  and and_7 (and_7_out, abcde_1_a, abcde_1_b);
  and and_8 (and_8_out, ~abcde_1_a, ~abcde_1_b);  // And
  and and_9 (and_9_out, abcde_1_a, ~abcde_1_b);  // And
  and and_10 (and_10_out, abcde_1_c, abcde_1_d);
  and and_11 (and_11_out, ~abcde_1_c, ~abcde_1_d);  // And
  and and_12 (and_12_out, abcde_1_c, ~abcde_1_d);  // And
  not not_1 (not_1_out, abcde_1_e);
  LED \SEMÁFORO_1  (.in(and_7_out));
  LED \SEMÁFORO_1_2  (.in(and_8_out));
  LED \SEMÁFORO_1_3  (.in(and_9_out));
  LED \SEMÁFORO_3  (.in(and_7_out));
  LED \SEMÁFORO_3_2  (.in(and_8_out));
  LED \SEMÁFORO_3_3  (.in(and_9_out));
  LED \SEMÁFORO_2  (.in(and_10_out));
  LED \SEMÁFORO_2_2  (.in(and_11_out));
  LED \SEMÁFORO_2_3  (.in(and_12_out));
  LED \SEMÁFORO_4  (.in(not_1_out));
  LED \SEMÁFORO_4_2  (.in(abcde_1_e));
  LED \SEMÁFORO_5  (.in(not_1_out));
  LED \SEMAFÓRO_5  (.in(abcde_1_e));
endmodule
