// Logisim project processador.circ as structural Verilog: 17 circuits, main circuit main
module main (
);

  wire clock_1_out, H, J, memoria_de_controle_1_branch, memoria_de_controle_1_i, memoria_de_controle_1_show,
       memoria_de_controle_1_we, or_1_out, ula_1_zero, ZB;
  wire [2:0] memoria_de_controle_1_ula;
  wire [15:0] SE;
  wire [23:0] multiplexer_1_out, register_1_q, S, signed_extension_1_s;
  wire [31:0] banco_de_registradores_1_a, banco_de_registradores_1_b, demultiplexer_1_out1,
       multiplexer_2_out, U;
  wire [31:16] rom_1_data;

  Register #(.width(24)) register_1 (.D(S), .en(H), .clk(clock_1_out), .Q(register_1_q));  // open: clr
  Clock clock_1 (.out(clock_1_out));
  SIGNED_EXTENSION signed_extension_1 (.E(SE), .S(signed_extension_1_s));
  or or_1 (or_1_out, ZB, J);
  ROM #(.addrWidth(24), .dataWidth(32)) rom_1 (.addr(register_1_q), .data({rom_1_data, SE}));
  Multiplexer #(.width(24)) multiplexer_1 (
    .in0(24'h1), .in1(signed_extension_1_s), .out(multiplexer_1_out), .sel(or_1_out));
  SOMADOR_SELETOR_24bits somador_seletor_24bits_1 (.A(multiplexer_1_out), .B(register_1_q), .Cin(1'b0), .S(S));
  MEMORIA_DE_CONTROLE memoria_de_controle_1 (
    .A(rom_1_data[31:28]), .ULA(memoria_de_controle_1_ula), .I(memoria_de_controle_1_i),
    .Show(memoria_de_controle_1_show), .WE(memoria_de_controle_1_we), .Branch(memoria_de_controle_1_branch),
    .Jump(J), .Halt(H));
  BANCO_DE_REGISTRADORES banco_de_registradores_1 (
    .C(U), .a1(rom_1_data[27:24]), .CLK(clock_1_out), .c1(rom_1_data[19:16]), .b1(rom_1_data[23:20]),
    .WE(memoria_de_controle_1_we), .A(banco_de_registradores_1_a), .B(banco_de_registradores_1_b));
  Demultiplexer #(.width(32)) demultiplexer_1 (
    .out1(demultiplexer_1_out1), .in(banco_de_registradores_1_a), .sel(memoria_de_controle_1_show));  // open: out0
  Multiplexer #(.width(32)) multiplexer_2 (
    .in0(banco_de_registradores_1_b), .in1({{16{1'b0}}, SE}), .out(multiplexer_2_out),
    .sel(memoria_de_controle_1_i));
  and and_1 (ZB, memoria_de_controle_1_branch, ula_1_zero);
  Hex_Digit_Display hex_digit_display_1 (.value(demultiplexer_1_out1[31:28]));  // open: dp
  Hex_Digit_Display hex_digit_display_2 (.value(demultiplexer_1_out1[27:24]));  // open: dp
  Hex_Digit_Display hex_digit_display_3 (.value(demultiplexer_1_out1[23:20]));  // open: dp
  Hex_Digit_Display hex_digit_display_4 (.value(demultiplexer_1_out1[19:16]));  // open: dp
  Hex_Digit_Display hex_digit_display_5 (.value(demultiplexer_1_out1[15:12]));  // open: dp
  Hex_Digit_Display hex_digit_display_6 (.value(demultiplexer_1_out1[11:8]));  // open: dp
  ULA ula_1 (
    .A(banco_de_registradores_1_a), .B(multiplexer_2_out), .OP(memoria_de_controle_1_ula), .ZERO(ula_1_zero),
    .S(U));
  Hex_Digit_Display hex_digit_display_7 (.value(demultiplexer_1_out1[7:4]));  // open: dp
  Hex_Digit_Display hex_digit_display_8 (.value(demultiplexer_1_out1[3:0]));  // open: dp

  // Notes on the sheet:
  //   contents of rom_1 (hex, n*v repeats v):
  //   0 b0010002 b0020001 11230000 c3000000 21240000 c4000000 31250000 c5000000 41260000 c6000000 51270000
  //   c7000000 62080000 c8000000 71290000 c9000000 812a0000 ca000000 920b0001 cb000000 a20c0001 cc000000
  //   e2100003 b2020001 d000fffe f0000000
endmodule

module ULA (
  input  [31:0] A,
  input  [31:0] B,
  input  [2:0] OP,
  output ZERO,
  output [31:0] S
);

  wire multiplexer_1_out;
  wire [31:0] and_1_out, demultiplexer_1_out0, demultiplexer_1_out1, not_1_out, not_2_out, or_1_out,
       shifter_32bits_1_s, somador_seletor_32bits_1_s, somador_seletor_32bits_2_s, xor_1_out;

  Multiplexer #(.select(3)) multiplexer_1 (
    .in0(1'b0), .in1(1'b0), .in2(1'b0), .in3(1'b0), .in4(1'b0), .in5(1'b0), .in6(1'b0), .in7(1'b1),
    .out(multiplexer_1_out), .sel(OP));
  assign not_1_out = ~B;  // NOT_Gate not_1, 32 bits wide
  assign and_1_out = A & B;  // AND_Gate and_1, 32 bits wide
  assign or_1_out = A | B;  // OR_Gate or_1, 32 bits wide
  assign xor_1_out = A ^ B;  // XOR_Gate xor_1, 32 bits wide
  assign not_2_out = ~A;  // NOT_Gate not_2, 32 bits wide
  SHIFTER_32bits shifter_32bits_1 (.D(multiplexer_1_out), .A(A), .B(B), .S(shifter_32bits_1_s));
  SOMADOR_SELETOR_32bits somador_seletor_32bits_1 (.A(A), .B(B), .Cin(1'b0), .S(somador_seletor_32bits_1_s));
  SOMADOR_SELETOR_32bits somador_seletor_32bits_2 (.A(A), .B(not_1_out), .Cin(1'b1), .S(somador_seletor_32bits_2_s));
  Demultiplexer #(.width(32)) demultiplexer_1 (
    .out0(demultiplexer_1_out0), .out1(demultiplexer_1_out1), .in(shifter_32bits_1_s), .sel(multiplexer_1_out));
  Multiplexer #(.select(3), .width(32)) multiplexer_2 (
    .in0(somador_seletor_32bits_1_s), .in1(somador_seletor_32bits_2_s), .in2(and_1_out), .in3(or_1_out),
    .in4(xor_1_out), .in5(not_2_out), .in6(demultiplexer_1_out0), .in7(demultiplexer_1_out1), .out(S),
    .sel(OP));
  VERIFICA_ZERO verifica_zero_1 (.A(somador_seletor_32bits_2_s), .S(ZERO));
endmodule

module BANCO_DE_REGISTRADORES (
  input  [31:0] C,
  input  [3:0] a1,
  input  CLK,
  input  [3:0] c1,
  input  [3:0] b1,
  input  WE,
  output [31:0] A,
  output [31:0] B
);

  wire demultiplexer_1_out0, demultiplexer_1_out1, demultiplexer_1_out2, demultiplexer_1_out3,
       demultiplexer_1_out4, demultiplexer_1_out5, demultiplexer_1_out6, demultiplexer_1_out7,
       demultiplexer_1_out8, demultiplexer_1_out9, demultiplexer_1_out10, demultiplexer_1_out11,
       demultiplexer_1_out12, demultiplexer_1_out13, demultiplexer_1_out14, demultiplexer_1_out15;
  wire [31:0] R0, R1, R2, R3, R4, R5, R6, R7, R8, R9, R10, R11, R12, R13, R14, R15;

  Demultiplexer #(.select(4)) demultiplexer_1 (
    .out0(demultiplexer_1_out0), .out1(demultiplexer_1_out1), .out2(demultiplexer_1_out2),
    .out3(demultiplexer_1_out3), .out4(demultiplexer_1_out4), .out5(demultiplexer_1_out5),
    .out6(demultiplexer_1_out6), .out7(demultiplexer_1_out7), .out8(demultiplexer_1_out8),
    .out9(demultiplexer_1_out9), .out10(demultiplexer_1_out10), .out11(demultiplexer_1_out11),
    .out12(demultiplexer_1_out12), .out13(demultiplexer_1_out13), .out14(demultiplexer_1_out14),
    .out15(demultiplexer_1_out15), .in(CLK), .sel(c1));
  Register #(.width(32)) register_1 (.D({32{1'b0}}), .en(WE), .clk(demultiplexer_1_out0), .Q(R0));  // open: clr
  Register #(.width(32)) register_2 (.D(C), .en(WE), .clk(demultiplexer_1_out1), .Q(R1));  // open: clr
  Register #(.width(32)) register_3 (.D(C), .en(WE), .clk(demultiplexer_1_out2), .Q(R2));  // open: clr
  Register #(.width(32)) register_4 (.D(C), .en(WE), .clk(demultiplexer_1_out3), .Q(R3));  // open: clr
  Register #(.width(32)) register_5 (.D(C), .en(WE), .clk(demultiplexer_1_out4), .Q(R4));  // open: clr
  Register #(.width(32)) register_6 (.D(C), .en(WE), .clk(demultiplexer_1_out5), .Q(R5));  // open: clr
  Register #(.width(32)) register_7 (.D(C), .en(WE), .clk(demultiplexer_1_out6), .Q(R6));  // open: clr
  Register #(.width(32)) register_8 (.D(C), .en(WE), .clk(demultiplexer_1_out7), .Q(R7));  // open: clr
  Register #(.width(32)) register_9 (.D(C), .en(WE), .clk(demultiplexer_1_out8), .Q(R8));  // open: clr
  Register #(.width(32)) register_10 (.D(C), .en(WE), .clk(demultiplexer_1_out9), .Q(R9));  // open: clr
  Register #(.width(32)) register_11 (.D(C), .en(WE), .clk(demultiplexer_1_out10), .Q(R10));  // open: clr
  Register #(.width(32)) register_12 (.D(C), .en(WE), .clk(demultiplexer_1_out11), .Q(R11));  // open: clr
  Register #(.width(32)) register_13 (.D(C), .en(WE), .clk(demultiplexer_1_out12), .Q(R12));  // open: clr
  Register #(.width(32)) register_14 (.D(C), .en(WE), .clk(demultiplexer_1_out13), .Q(R13));  // open: clr
  Register #(.width(32)) register_15 (.D(C), .en(WE), .clk(demultiplexer_1_out14), .Q(R14));  // open: clr
  Register #(.width(32)) register_16 (.D(C), .en(WE), .clk(demultiplexer_1_out15), .Q(R15));  // open: clr
  Multiplexer #(.select(4), .width(32)) multiplexer_1 (
    .in0(R0), .in1(R1), .in2(R2), .in3(R3), .in4(R4), .in5(R5), .in6(R6), .in7(R7), .in8(R8), .in9(R9),
    .in10(R10), .in11(R11), .in12(R12), .in13(R13), .in14(R14), .in15(R15), .out(A), .sel(a1));
  Multiplexer #(.select(4), .width(32)) multiplexer_2 (
    .in0(R0), .in1(R1), .in2(R2), .in3(R3), .in4(R4), .in5(R5), .in6(R6), .in7(R7), .in8(R8), .in9(R9),
    .in10(R10), .in11(R11), .in12(R12), .in13(R13), .in14(R14), .in15(R15), .out(B), .sel(b1));
endmodule

module MEMORIA_DE_CONTROLE (
  input  [3:0] A,
  output [2:0] ULA,
  output I,
  output Show,
  output WE,
  output Branch,
  output Jump,
  output Halt
);

  ROM #(.addrWidth(4), .dataWidth(9)) rom_1 (.addr(A), .data({Halt, Jump, Branch, WE, Show, I, ULA}));

  // Notes on the sheet:
  //   contents of rom_1 (hex, n*v repeats v):
  //   100 120 121 122 123 124 125 126 127 12b 12c 128 110 180 140
endmodule

module SIGNED_EXTENSION (
  input  [15:0] E,
  output [23:0] S
);


  assign S = {{9{E[15]}}, E[14:0]};
endmodule

module FULL_ADDER (
  input  A,
  input  B,
  input  Cin,
  output S,
  output Cout
);

  wire and_1_out, and_2_out, xor_1_out;

  xor xor_1 (xor_1_out, A, B);
  and and_1 (and_1_out, xor_1_out, Cin);
  and and_2 (and_2_out, A, B);
  xor xor_2 (S, xor_1_out, Cin);
  xor xor_3 (Cout, and_1_out, and_2_out);
endmodule

module SOMADOR_4bits (
  input  [3:0] A,
  input  [3:0] B,
  input  Cin,
  output Cout,
  output [3:0] S
);

  wire full_adder_1_cout, full_adder_2_cout, full_adder_3_cout;

  FULL_ADDER full_adder_1 (.A(A[0]), .B(B[0]), .Cin(Cin), .S(S[0]), .Cout(full_adder_1_cout));
  FULL_ADDER full_adder_2 (.A(A[1]), .B(B[1]), .Cin(full_adder_1_cout), .S(S[1]), .Cout(full_adder_2_cout));
  FULL_ADDER full_adder_3 (.A(A[2]), .B(B[2]), .Cin(full_adder_2_cout), .S(S[2]), .Cout(full_adder_3_cout));
  FULL_ADDER full_adder_4 (.A(A[3]), .B(B[3]), .Cin(full_adder_3_cout), .S(S[3]), .Cout(Cout));
endmodule

module SOMADOR_SELETOR_4bits (
  input  [3:0] A,
  input  [3:0] B,
  input  Cin,
  output Cout,
  output [3:0] S
);

  wire Cout0, Cout1, full_adder_1_cout, full_adder_2_cout, full_adder_3_cout, full_adder_4_cout,
       full_adder_5_cout, full_adder_6_cout;
  wire [3:0] S0, S1;

  FULL_ADDER full_adder_1 (.A(A[0]), .B(B[0]), .Cin(1'b0), .S(S0[0]), .Cout(full_adder_1_cout));
  FULL_ADDER full_adder_2 (.A(A[0]), .B(B[0]), .Cin(1'b1), .S(S1[0]), .Cout(full_adder_2_cout));
  FULL_ADDER full_adder_3 (.A(A[1]), .B(B[1]), .Cin(full_adder_1_cout), .S(S0[1]), .Cout(full_adder_3_cout));
  FULL_ADDER full_adder_4 (.A(A[1]), .B(B[1]), .Cin(full_adder_2_cout), .S(S1[1]), .Cout(full_adder_4_cout));
  FULL_ADDER full_adder_5 (.A(A[2]), .B(B[2]), .Cin(full_adder_3_cout), .S(S0[2]), .Cout(full_adder_5_cout));
  FULL_ADDER full_adder_6 (.A(A[2]), .B(B[2]), .Cin(full_adder_4_cout), .S(S1[2]), .Cout(full_adder_6_cout));
  FULL_ADDER full_adder_7 (.A(A[3]), .B(B[3]), .Cin(full_adder_5_cout), .S(S0[3]), .Cout(Cout0));
  FULL_ADDER full_adder_8 (.A(A[3]), .B(B[3]), .Cin(full_adder_6_cout), .S(S1[3]), .Cout(Cout1));
  Multiplexer multiplexer_1 (.in0(Cout0), .in1(Cout1), .out(Cout), .sel(Cin));
  Multiplexer #(.width(4)) multiplexer_2 (.in0(S0), .in1(S1), .out(S), .sel(Cin));

  // Other names for the same wires on the sheet: TCin = Cin
endmodule

module SOMADOR_SELETOR_24bits (
  input  [23:0] A,
  input  [23:0] B,
  input  Cin,
  output [23:0] S
);

  wire somador_4bits_1_cout, somador_seletor_4bits_2_cout, somador_seletor_4bits_3_cout,
       somador_seletor_4bits_4_cout, somador_seletor_4bits_5_cout;

  SOMADOR_SELETOR_4bits somador_seletor_4bits_1 (
    .A(A[23:20]), .B(B[23:20]), .Cin(somador_seletor_4bits_2_cout), .S(S[23:20]));  // open: Cout
  SOMADOR_SELETOR_4bits somador_seletor_4bits_2 (
    .A(A[19:16]), .B(B[19:16]), .Cin(somador_seletor_4bits_3_cout), .Cout(somador_seletor_4bits_2_cout),
    .S(S[19:16]));
  SOMADOR_SELETOR_4bits somador_seletor_4bits_3 (
    .A(A[15:12]), .B(B[15:12]), .Cin(somador_seletor_4bits_4_cout), .Cout(somador_seletor_4bits_3_cout),
    .S(S[15:12]));
  SOMADOR_SELETOR_4bits somador_seletor_4bits_4 (
    .A(A[11:8]), .B(B[11:8]), .Cin(somador_seletor_4bits_5_cout), .Cout(somador_seletor_4bits_4_cout),
    .S(S[11:8]));
  SOMADOR_SELETOR_4bits somador_seletor_4bits_5 (
    .A(A[7:4]), .B(B[7:4]), .Cin(somador_4bits_1_cout), .Cout(somador_seletor_4bits_5_cout), .S(S[7:4]));
  SOMADOR_4bits somador_4bits_1 (.A(A[3:0]), .B(B[3:0]), .Cin(Cin), .Cout(somador_4bits_1_cout), .S(S[3:0]));
endmodule

module SOMADOR_SELETOR_32bits (
  input  [31:0] A,
  input  [31:0] B,
  input  Cin,
  output [31:0] S
);

  wire somador_4bits_1_cout, somador_seletor_4bits_2_cout, somador_seletor_4bits_3_cout,
       somador_seletor_4bits_4_cout, somador_seletor_4bits_5_cout, somador_seletor_4bits_6_cout,
       somador_seletor_4bits_7_cout;

  SOMADOR_SELETOR_4bits somador_seletor_4bits_1 (
    .A(A[31:28]), .B(B[31:28]), .Cin(somador_seletor_4bits_2_cout), .S(S[31:28]));  // open: Cout
  SOMADOR_SELETOR_4bits somador_seletor_4bits_2 (
    .A(A[27:24]), .B(B[27:24]), .Cin(somador_seletor_4bits_3_cout), .Cout(somador_seletor_4bits_2_cout),
    .S(S[27:24]));
  SOMADOR_SELETOR_4bits somador_seletor_4bits_3 (
    .A(A[23:20]), .B(B[23:20]), .Cin(somador_seletor_4bits_4_cout), .Cout(somador_seletor_4bits_3_cout),
    .S(S[23:20]));
  SOMADOR_SELETOR_4bits somador_seletor_4bits_4 (
    .A(A[19:16]), .B(B[19:16]), .Cin(somador_seletor_4bits_5_cout), .Cout(somador_seletor_4bits_4_cout),
    .S(S[19:16]));
  SOMADOR_SELETOR_4bits somador_seletor_4bits_5 (
    .A(A[15:12]), .B(B[15:12]), .Cin(somador_seletor_4bits_6_cout), .Cout(somador_seletor_4bits_5_cout),
    .S(S[15:12]));
  SOMADOR_SELETOR_4bits somador_seletor_4bits_6 (
    .A(A[11:8]), .B(B[11:8]), .Cin(somador_seletor_4bits_7_cout), .Cout(somador_seletor_4bits_6_cout),
    .S(S[11:8]));
  SOMADOR_SELETOR_4bits somador_seletor_4bits_7 (
    .A(A[7:4]), .B(B[7:4]), .Cin(somador_4bits_1_cout), .Cout(somador_seletor_4bits_7_cout), .S(S[7:4]));
  SOMADOR_4bits somador_4bits_1 (.A(A[3:0]), .B(B[3:0]), .Cin(Cin), .Cout(somador_4bits_1_cout), .S(S[3:0]));
endmodule

module SHIFTER_1bit (
  input  [31:0] A,
  input  D,
  input  E,
  output [31:0] S
);

  wire [31:0] multiplexer_1_out;

  Multiplexer #(.width(32)) multiplexer_1 (
    .in0({A[30:0], 1'b0}), .in1({1'b0, A[31:1]}), .out(multiplexer_1_out), .sel(D));
  Multiplexer #(.width(32)) multiplexer_2 (.in0(A), .in1(multiplexer_1_out), .out(S), .sel(E));
endmodule

module SHIFTER_2bits (
  input  [31:0] A,
  input  D,
  input  E,
  output [31:0] S
);

  wire [31:0] multiplexer_1_out;

  Multiplexer #(.width(32)) multiplexer_1 (
    .in0({A[29:0], 2'b00}), .in1({2'b00, A[31:2]}), .out(multiplexer_1_out), .sel(D));
  Multiplexer #(.width(32)) multiplexer_2 (.in0(A), .in1(multiplexer_1_out), .out(S), .sel(E));
endmodule

module SHIFTER_4bits (
  input  [31:0] A,
  input  D,
  input  E,
  output [31:0] S
);

  wire [31:0] multiplexer_1_out;

  Multiplexer #(.width(32)) multiplexer_1 (
    .in0({A[27:0], 4'b0000}), .in1({4'b0000, A[31:4]}), .out(multiplexer_1_out), .sel(D));
  Multiplexer #(.width(32)) multiplexer_2 (.in0(A), .in1(multiplexer_1_out), .out(S), .sel(E));
endmodule

module SHIFTER_8bits (
  input  [31:0] A,
  input  D,
  input  E,
  output [31:0] S
);

  wire [31:0] multiplexer_1_out;

  Multiplexer #(.width(32)) multiplexer_1 (
    .in0({A[23:0], {8{1'b0}}}), .in1({{8{1'b0}}, A[31:8]}), .out(multiplexer_1_out), .sel(D));
  Multiplexer #(.width(32)) multiplexer_2 (.in0(A), .in1(multiplexer_1_out), .out(S), .sel(E));
endmodule

module SHIFTER_16bits (
  input  [31:0] A,
  input  D,
  input  E,
  output [31:0] S
);

  wire [31:0] multiplexer_1_out;

  Multiplexer #(.width(32)) multiplexer_1 (
    .in0({A[15:0], {16{1'b0}}}), .in1({{16{1'b0}}, A[31:16]}), .out(multiplexer_1_out), .sel(D));
  Multiplexer #(.width(32)) multiplexer_2 (.in0(A), .in1(multiplexer_1_out), .out(S), .sel(E));
endmodule

module SHIFTER_32bits (
  input  D,
  input  [31:0] A,
  input  [31:0] B,
  output [31:0] S
);

  wire or_1_out;
  wire [31:0] shifter_1bit_1_s, shifter_2bits_1_s, shifter_4bits_1_s, shifter_8bits_1_s, shifter_16bits_1_s;

  SHIFTER_1bit shifter_1bit_1 (.A(A), .D(D), .E(B[0]), .S(shifter_1bit_1_s));
  or or_1 (or_1_out, B[5], B[6], B[7], B[8], B[9], B[10], B[11], B[12], B[13], B[14], B[15], B[16], B[17], B[18], B[19], B[20], B[21], B[22], B[23], B[24], B[25], B[26], B[27], B[28], B[29], B[30], B[31]);
  SHIFTER_2bits shifter_2bits_1 (.A(shifter_1bit_1_s), .D(D), .E(B[1]), .S(shifter_2bits_1_s));
  SHIFTER_4bits shifter_4bits_1 (.A(shifter_2bits_1_s), .D(D), .E(B[2]), .S(shifter_4bits_1_s));
  SHIFTER_8bits shifter_8bits_1 (.A(shifter_4bits_1_s), .D(D), .E(B[3]), .S(shifter_8bits_1_s));
  SHIFTER_16bits shifter_16bits_1 (.A(shifter_8bits_1_s), .D(D), .E(B[4]), .S(shifter_16bits_1_s));
  Multiplexer #(.width(32)) multiplexer_1 (.in0(shifter_16bits_1_s), .in1({32{1'b0}}), .out(S), .sel(or_1_out));
endmodule

module VERIFICA_ZERO (
  input  [31:0] A,
  output S
);

  nor nor_1 (S, A[0], A[1], A[2], A[3], A[4], A[5], A[6], A[7], A[8], A[9], A[10], A[11], A[12], A[13], A[14], A[15], A[16], A[17], A[18], A[19], A[20], A[21], A[22], A[23], A[24], A[25], A[26], A[27], A[28], A[29], A[30], A[31]);
endmodule
