// Logisim project sagui.circ as structural Verilog: 7 circuits, main circuit main
module main (
);

  wire and_1_out, and_2_out, brzi, brzr, CLK, ji, jr, memcontrol_1_load, memcontrol_1_movh,
       memcontrol_1_movl, memcontrol_1_store, or_1_out, or_2_out, or_3_out, RW, Z;
  wire [1:0] multiplexer_4_out;
  wire [2:0] memcontrol_1_alu;
  wire [7:0] adder_1_out, B, D, M, memdata_1_d, multiplexer_1_out, multiplexer_2_out, multiplexer_3_out,
       multiplexer_6_out, PC_q, regbank_1_a, regbank_1_r0, SE, ula_1_d;
  wire [7:4] meminstruction_1_instruction, meminstruction_1_instruction_2;

  Multiplexer #(.width(8)) multiplexer_1 (.in0(8'h1), .in1(SE), .out(multiplexer_1_out), .sel(or_1_out));
  or or_1 (or_1_out, ji, and_1_out);
  and and_1 (and_1_out, brzi, Z);
  Adder adder_1 (.a(PC_q), .b(multiplexer_1_out), .out(adder_1_out));  // open: cin, cout
  Multiplexer #(.width(8)) multiplexer_2 (.in0(adder_1_out), .in1(B), .out(multiplexer_2_out), .sel(or_2_out));
  or or_2 (or_2_out, jr, and_2_out);
  Clock clock_1 (.out(CLK));
  and and_2 (and_2_out, brzr, Z);
  Register PC (.D(multiplexer_2_out), .en(CLK), .clk(CLK), .Q(PC_q));  // open: clr
  MemInstruction meminstruction_1 (
    .PC(PC_q), .Instruction({meminstruction_1_instruction, meminstruction_1_instruction_2}));
  Multiplexer #(.width(8)) multiplexer_3 (.in0(D), .in1(M), .out(multiplexer_3_out), .sel(or_3_out));
  MemControl memcontrol_1 (
    .A(meminstruction_1_instruction), .brzr(brzr), .brzi(brzi), .ji(ji), .jr(jr), .Movh(memcontrol_1_movh),
    .Movl(memcontrol_1_movl), .RegWrite(RW), .Store(memcontrol_1_store), .Load(memcontrol_1_load),
    .ALU(memcontrol_1_alu));
  Multiplexer #(.width(2)) multiplexer_4 (
    .in0(meminstruction_1_instruction_2[7:6]), .in1(2'b00), .out(multiplexer_4_out), .sel(or_3_out));
  or or_3 (or_3_out, memcontrol_1_movh, memcontrol_1_movl);
  assign SE = {{4{meminstruction_1_instruction_2[7]}}, meminstruction_1_instruction_2};  // Bit_Extender bit_extender_1
  RegBank regbank_1 (
    .D(multiplexer_3_out), .WE(RW), .Ra(meminstruction_1_instruction_2[7:6]), .Rd(multiplexer_4_out),
    .CLK(CLK), .Rb(meminstruction_1_instruction_2[5:4]), .R0(regbank_1_r0), .A(regbank_1_a), .B(B));
  Multiplexer #(.width(8)) multiplexer_5 (
    .in0({meminstruction_1_instruction_2, regbank_1_r0[3:0]}),
    .in1({regbank_1_r0[7:4], meminstruction_1_instruction_2}), .out(M), .sel(memcontrol_1_movl));
  Multiplexer #(.width(8)) multiplexer_6 (.in0(regbank_1_a), .in1(regbank_1_r0), .out(multiplexer_6_out), .sel(brzi));
  IsZero iszero_1 (.A(multiplexer_6_out), .Z(Z));
  ULA ula_1 (.A(regbank_1_a), .B(B), .OP(memcontrol_1_alu), .D(ula_1_d));
  MemData memdata_1 (.B(B), .S(memcontrol_1_store), .CLK(CLK), .A(regbank_1_a), .D(memdata_1_d));
  Multiplexer #(.width(8)) multiplexer_7 (.in0(ula_1_d), .in1(memdata_1_d), .out(D), .sel(memcontrol_1_load));
endmodule

module ULA (
  input  [7:0] A,
  input  [7:0] B,
  input  [2:0] OP,
  output [7:0] D
);

  wire or_1_out;
  wire [2:0] multiplexer_1_out;
  wire [7:0] adder_1_out, and_1_out, not_1_out, or_2_out, shifter_1_out, shifter_2_out, subtractor_1_out;

  or or_1 (or_1_out, B[3], B[4], B[5], B[6], B[7]);
  Multiplexer #(.width(3)) multiplexer_1 (.in0(B[2:0]), .in1(3'b000), .out(multiplexer_1_out), .sel(or_1_out));
  Adder adder_1 (.a(A), .b(B), .out(adder_1_out));  // open: cin, cout
  Subtractor subtractor_1 (.a(A), .b(B), .out(subtractor_1_out));  // open: bin, bout
  assign and_1_out = A & B;  // AND_Gate and_1, 8 bits wide
  assign or_2_out = A | B;  // OR_Gate or_2, 8 bits wide
  assign not_1_out = ~B;  // NOT_Gate not_1, 8 bits wide
  Shifter shifter_1 (.in(A), .\dist (multiplexer_1_out), .out(shifter_1_out));
  Shifter #(.shift("lr")) shifter_2 (.in(A), .\dist (multiplexer_1_out), .out(shifter_2_out));
  Multiplexer #(.select(3), .width(8)) multiplexer_2 (
    .in0(B), .in1(adder_1_out), .in2(subtractor_1_out), .in3(and_1_out), .in4(or_2_out), .in5(not_1_out),
    .in6(shifter_1_out), .in7(shifter_2_out), .out(D), .sel(OP));
endmodule

module IsZero (
  input  [7:0] A,
  output Z
);

  nor nor_1 (Z, A[0], A[1], A[2], A[3], A[4], A[5], A[6], A[7]);
endmodule

module RegBank (
  input  [7:0] D,
  input  WE,
  input  [1:0] Ra,
  input  [1:0] Rd,
  input  CLK,
  input  [1:0] Rb,
  output [7:0] R0,
  output [7:0] A,
  output [7:0] B
);

  wire demultiplexer_1_out0, demultiplexer_1_out1, demultiplexer_1_out2, demultiplexer_1_out3;
  wire [7:0] R1, R2, R3;

  Demultiplexer #(.select(2)) demultiplexer_1 (
    .out0(demultiplexer_1_out0), .out1(demultiplexer_1_out1), .out2(demultiplexer_1_out2),
    .out3(demultiplexer_1_out3), .in(WE), .sel(Rd));
  Register register_1 (.D(D), .en(demultiplexer_1_out0), .clk(CLK), .Q(R0));  // open: clr
  Register register_2 (.D(D), .en(demultiplexer_1_out1), .clk(CLK), .Q(R1));  // open: clr
  Register register_3 (.D(D), .en(demultiplexer_1_out2), .clk(CLK), .Q(R2));  // open: clr
  Register register_4 (.D(D), .en(demultiplexer_1_out3), .clk(CLK), .Q(R3));  // open: clr
  Multiplexer #(.select(2), .width(8)) multiplexer_1 (.in0(R0), .in1(R1), .in2(R2), .in3(R3), .out(A), .sel(Ra));
  Multiplexer #(.select(2), .width(8)) multiplexer_2 (.in0(R0), .in1(R1), .in2(R2), .in3(R3), .out(B), .sel(Rb));
endmodule

module MemControl (
  input  [3:0] A,
  output brzr,
  output brzi,
  output ji,
  output jr,
  output Movh,
  output Movl,
  output RegWrite,
  output Store,
  output Load,
  output [2:0] ALU
);

  ROM #(.addrWidth(4), .dataWidth(12)) rom_1 (
    .addr(A), .data({brzr, brzi, ji, jr, Movh, Movl, RegWrite, Store, Load, ALU}));

  // Notes on the sheet:
  //   contents of rom_1 (hex, n*v repeats v):
  //   800 400 100 200 28 10 20 a1 61 21 22 23 24 25 26 27
endmodule

module MemData (
  input  [7:0] B,
  input  S,
  input  CLK,
  input  [7:0] A,
  output [7:0] D
);

  RAM #(.enables("line")) ram_1 (.addr(B), .we(S), .clk(CLK), .din(A), .dout(D));
endmodule

module MemInstruction (
  input  [7:0] PC,
  output [7:0] Instruction
);

  ROM rom_1 (.addr(PC), .data(Instruction));

  // Notes on the sheet:
  //   contents of rom_1 (hex, n*v repeats v):
  //   81 64 74 98 e1 6c 87 b a9 20 b5 c5 80 d4 81 68 5c 42 f2 13 a2 3e 20
endmodule
