// Logisim project saguiVetorial.circ as structural Verilog: 9 circuits, main circuit main
module main (
);

  wire and_1_out, Br, CLK, L, Low, Move, S, scalarmemcontrol_1_load, scalarmemcontrol_1_low,
       scalarmemcontrol_1_move, scalarmemcontrol_1_regwrite, scalarmemcontrol_1_store,
       vectormemcontrol_1_regwrite, Z;
  wire [1:0] decode_1_s_2, decode_1_s_3, multiplexer_7_out, multiplexer_8_out, multiplexer_9_out,
       multiplexer_10_out, multiplexer_11_out, OP, scalarmemcontrol_1_aluop;
  wire [3:0] I;
  wire [6:4] decode_1_s, decode_1_v;
  wire [7:0] adder_1_out, B, D, D0, D1, D2, D3, memdata_1_d, memdata_2_d, memdata_3_d, memdata_4_d,
       memdata_5_d, multiplexer_1_out, multiplexer_2_out, multiplexer_3_out, multiplexer_4_out,
       multiplexer_5_out, multiplexer_6_out, multiplexer_12_out, multiplexer_13_out, multiplexer_14_out,
       multiplexer_15_out, multiplexer_16_out, regbank_1_a, regbank_1_r1, regbank_2_a, regbank_2_b,
       regbank_2_r1, regbank_3_a, regbank_3_b, regbank_3_r1, regbank_4_a, regbank_4_b, regbank_4_r1,
       regbank_5_a, regbank_5_b, regbank_5_r1, register_1_q, rom_1_data, S1, scalarula_1_d, V0, V1, V2, V3,
       vectorula_1_d, vectorula_2_d, vectorula_3_d, vectorula_4_d;

  Adder adder_1 (.a(register_1_q), .b(8'h1), .out(adder_1_out));  // open: cin, cout
  Multiplexer #(.width(8)) multiplexer_1 (.in0(adder_1_out), .in1(B), .out(multiplexer_1_out), .sel(and_1_out));
  and and_1 (and_1_out, Br, Z);
  Register register_1 (.D(multiplexer_1_out), .en(1'b1), .clk(CLK), .Q(register_1_q));  // open: clr
  Clock clock_1 (.out(CLK));
  ROM rom_1 (.addr(register_1_q), .data(rom_1_data));
  Decode decode_1 (.IP(rom_1_data), .S({decode_1_s, decode_1_s_3, decode_1_s_2}), .V({decode_1_v, I}));
  Multiplexer #(.width(8)) multiplexer_2 (.in0(D0), .in1(V0), .out(multiplexer_2_out), .sel(Move));
  Multiplexer #(.width(8)) multiplexer_3 (.in0(D1), .in1(V1), .out(multiplexer_3_out), .sel(Move));
  Multiplexer #(.width(8)) multiplexer_4 (.in0(D2), .in1(V2), .out(multiplexer_4_out), .sel(Move));
  Multiplexer #(.width(8)) multiplexer_5 (.in0(D3), .in1(V3), .out(multiplexer_5_out), .sel(Move));
  VectorMemControl vectormemcontrol_1 (
    .OpCode(decode_1_v), .Move(Move), .Low(Low), .Store(S), .Load(L), .RegWrite(vectormemcontrol_1_regwrite),
    .ALUop(OP));
  Multiplexer #(.width(8)) multiplexer_6 (.in0(D), .in1(S1), .out(multiplexer_6_out), .sel(scalarmemcontrol_1_move));
  ScalarMemControl scalarmemcontrol_1 (
    .OpCode(decode_1_s), .Branch(Br), .Move(scalarmemcontrol_1_move), .Low(scalarmemcontrol_1_low),
    .Store(scalarmemcontrol_1_store), .Load(scalarmemcontrol_1_load), .RegWrite(scalarmemcontrol_1_regwrite),
    .ALUop(scalarmemcontrol_1_aluop));
  Multiplexer #(.width(2)) multiplexer_7 (.in0(I[3:2]), .in1(2'b01), .out(multiplexer_7_out), .sel(Move));
  Multiplexer #(.width(2)) multiplexer_8 (.in0(I[3:2]), .in1(2'b01), .out(multiplexer_8_out), .sel(Move));
  Multiplexer #(.width(2)) multiplexer_9 (.in0(I[3:2]), .in1(2'b01), .out(multiplexer_9_out), .sel(Move));
  Multiplexer #(.width(2)) multiplexer_10 (
    .in0(decode_1_s_3), .in1(2'b01), .out(multiplexer_10_out), .sel(scalarmemcontrol_1_move));
  Multiplexer #(.width(2)) multiplexer_11 (.in0(I[3:2]), .in1(2'b01), .out(multiplexer_11_out), .sel(Move));
  RegBank regbank_1 (
    .ID({8{1'b0}}), .D(multiplexer_6_out), .Ra(decode_1_s_3), .WE(scalarmemcontrol_1_regwrite),
    .Rd(multiplexer_10_out), .CLK(CLK), .Rb(decode_1_s_2), .R1(regbank_1_r1), .A(regbank_1_a), .B(B));
  RegBank regbank_2 (
    .ID({8{1'b0}}), .D(multiplexer_2_out), .Ra(I[3:2]), .WE(vectormemcontrol_1_regwrite),
    .Rd(multiplexer_7_out), .CLK(CLK), .Rb(I[1:0]), .R1(regbank_2_r1), .A(regbank_2_a), .B(regbank_2_b));
  RegBank regbank_3 (
    .ID(8'h1), .D(multiplexer_3_out), .Ra(I[3:2]), .WE(vectormemcontrol_1_regwrite), .Rd(multiplexer_8_out),
    .CLK(CLK), .Rb(I[1:0]), .R1(regbank_3_r1), .A(regbank_3_a), .B(regbank_3_b));
  RegBank regbank_4 (
    .ID(8'h2), .D(multiplexer_4_out), .Ra(I[3:2]), .WE(vectormemcontrol_1_regwrite), .Rd(multiplexer_9_out),
    .CLK(CLK), .Rb(I[1:0]), .R1(regbank_4_r1), .A(regbank_4_a), .B(regbank_4_b));
  RegBank regbank_5 (
    .ID(8'h3), .D(multiplexer_5_out), .Ra(I[3:2]), .WE(vectormemcontrol_1_regwrite), .Rd(multiplexer_11_out),
    .CLK(CLK), .Rb(I[1:0]), .R1(regbank_5_r1), .A(regbank_5_a), .B(regbank_5_b));
  Multiplexer #(.width(8)) multiplexer_12 (
    .in0({decode_1_s_3, decode_1_s_2, regbank_1_r1[3:0]}),
    .in1({regbank_1_r1[7:4], decode_1_s_3, decode_1_s_2}), .out(multiplexer_12_out),
    .sel(scalarmemcontrol_1_low));
  Multiplexer #(.width(8)) multiplexer_13 (
    .in0({I, regbank_2_r1[3:0]}), .in1({regbank_2_r1[7:4], I}), .out(multiplexer_13_out), .sel(Low));
  Multiplexer #(.width(8)) multiplexer_14 (
    .in0({I, regbank_3_r1[3:0]}), .in1({regbank_3_r1[7:4], I}), .out(multiplexer_14_out), .sel(Low));
  Multiplexer #(.width(8)) multiplexer_15 (
    .in0({I, regbank_4_r1[3:0]}), .in1({regbank_4_r1[7:4], I}), .out(multiplexer_15_out), .sel(Low));
  Multiplexer #(.width(8)) multiplexer_16 (
    .in0({I, regbank_5_r1[3:0]}), .in1({regbank_5_r1[7:4], I}), .out(multiplexer_16_out), .sel(Low));
  Multiplexer #(.width(8)) multiplexer_17 (
    .in0(regbank_1_r1), .in1(multiplexer_12_out), .out(S1), .sel(scalarmemcontrol_1_move));
  Multiplexer #(.width(8)) multiplexer_18 (.in0(regbank_2_r1), .in1(multiplexer_13_out), .out(V0), .sel(Move));
  Multiplexer #(.width(8)) multiplexer_19 (.in0(regbank_3_r1), .in1(multiplexer_14_out), .out(V1), .sel(Move));
  Multiplexer #(.width(8)) multiplexer_20 (.in0(regbank_4_r1), .in1(multiplexer_15_out), .out(V2), .sel(Move));
  Multiplexer #(.width(8)) multiplexer_21 (.in0(regbank_5_r1), .in1(multiplexer_16_out), .out(V3), .sel(Move));
  VectorULA vectorula_1 (.A(regbank_2_a), .B(regbank_2_b), .OP(OP), .D(vectorula_1_d));
  Multiplexer #(.width(8)) multiplexer_22 (.in0(vectorula_1_d), .in1(memdata_1_d), .out(D0), .sel(L));
  MemData memdata_1 (.B(regbank_2_b), .S(S), .CLK(CLK), .A(regbank_2_a), .D(memdata_1_d));
  VectorULA vectorula_2 (.A(regbank_3_a), .B(regbank_3_b), .OP(OP), .D(vectorula_2_d));
  Multiplexer #(.width(8)) multiplexer_23 (.in0(vectorula_2_d), .in1(memdata_2_d), .out(D1), .sel(L));
  MemData memdata_2 (.B(regbank_3_b), .S(S), .CLK(CLK), .A(regbank_3_a), .D(memdata_2_d));
  VectorULA vectorula_3 (.A(regbank_4_a), .B(regbank_4_b), .OP(OP), .D(vectorula_3_d));
  Multiplexer #(.width(8)) multiplexer_24 (.in0(vectorula_3_d), .in1(memdata_3_d), .out(D2), .sel(L));
  MemData memdata_3 (.B(regbank_4_b), .S(S), .CLK(CLK), .A(regbank_4_a), .D(memdata_3_d));
  VectorULA vectorula_4 (.A(regbank_5_a), .B(regbank_5_b), .OP(OP), .D(vectorula_4_d));
  Multiplexer #(.width(8)) multiplexer_25 (.in0(vectorula_4_d), .in1(memdata_4_d), .out(D3), .sel(L));
  MemData memdata_4 (.B(regbank_5_b), .S(S), .CLK(CLK), .A(regbank_5_a), .D(memdata_4_d));
  IsZero iszero_1 (.A(regbank_1_a), .Z(Z));
  ScalarULA scalarula_1 (.A(regbank_1_a), .B(B), .OP(scalarmemcontrol_1_aluop), .D(scalarula_1_d));
  MemData memdata_5 (.B(B), .S(scalarmemcontrol_1_store), .CLK(CLK), .A(regbank_1_a), .D(memdata_5_d));
  Multiplexer #(.width(8)) multiplexer_26 (
    .in0(scalarula_1_d), .in1(memdata_5_d), .out(D), .sel(scalarmemcontrol_1_load));

  // Notes on the sheet:
  //   contents of rom_1 (hex, n*v repeats v):
  //   2f 3f 66 31 4d 15 9 56 af bf e6 b1 95 89 c6 d6 f6 75
endmodule

module Decode (
  input  [7:0] IP,
  output [6:0] S,
  output [6:0] V
);

  Demultiplexer #(.width(7)) demultiplexer_1 (.out0(S), .out1(V), .in(IP[6:0]), .sel(IP[7]));
endmodule

module RegBank (
  input  [7:0] ID,
  input  [7:0] D,
  input  [1:0] Ra,
  input  WE,
  input  [1:0] Rd,
  input  CLK,
  input  [1:0] Rb,
  output [7:0] R1,
  output [7:0] A,
  output [7:0] B
);

  wire demultiplexer_1_out1, demultiplexer_1_out2, demultiplexer_1_out3;
  wire [7:0] R2, R3;

  Demultiplexer #(.select(2)) demultiplexer_1 (
    .out1(demultiplexer_1_out1), .out2(demultiplexer_1_out2), .out3(demultiplexer_1_out3), .in(WE), .sel(Rd));  // open: out0
  Register register_1 (.D(D), .en(demultiplexer_1_out1), .clk(CLK), .Q(R1));  // open: clr
  Register register_2 (.D(D), .en(demultiplexer_1_out2), .clk(CLK), .Q(R2));  // open: clr
  Register register_3 (.D(D), .en(demultiplexer_1_out3), .clk(CLK), .Q(R3));  // open: clr
  Multiplexer #(.select(2), .width(8)) multiplexer_1 (.in0(ID), .in1(R1), .in2(R2), .in3(R3), .out(A), .sel(Ra));
  Multiplexer #(.select(2), .width(8)) multiplexer_2 (.in0(ID), .in1(R1), .in2(R2), .in3(R3), .out(B), .sel(Rb));

  // Other names for the same wires on the sheet: R0[7:0] = ID
endmodule

module MemData (
  input  [7:0] B,
  input  S,
  input  CLK,
  input  [7:0] A,
  output [7:0] D
);

  RAM #(.enables("line")) ram_1 (.addr(B), .we(S), .clk(CLK), .din(A), .dout(D));
endmodule

module ScalarMemControl (
  input  [2:0] OpCode,
  output Branch,
  output Move,
  output Low,
  output Store,
  output Load,
  output RegWrite,
  output [1:0] ALUop
);

  ROM #(.addrWidth(3)) rom_1 (.addr(OpCode), .data({Branch, Move, Low, Store, Load, RegWrite, ALUop}));

  // Notes on the sheet:
  //   contents of rom_1 (hex, n*v repeats v):
  //   c 10 44 64 4 5 6 80
endmodule

module ScalarULA (
  input  [7:0] A,
  input  [7:0] B,
  input  [1:0] OP,
  output [7:0] D
);

  wire [7:0] adder_1_out, and_1_out, subtractor_1_out;

  Adder adder_1 (.a(A), .b(B), .out(adder_1_out));  // open: cin, cout
  Subtractor subtractor_1 (.a(A), .b(B), .out(subtractor_1_out));  // open: bin, bout
  assign and_1_out = A & B;  // AND_Gate and_1, 8 bits wide
  Multiplexer #(.select(2), .width(8)) multiplexer_1 (
    .in0(adder_1_out), .in1(subtractor_1_out), .in2(and_1_out), .out(D), .sel(OP));  // open: in3
endmodule

module VectorMemControl (
  input  [2:0] OpCode,
  output Move,
  output Low,
  output Store,
  output Load,
  output RegWrite,
  output [1:0] ALUop
);

  ROM #(.addrWidth(3), .dataWidth(7)) rom_1 (.addr(OpCode), .data({Move, Low, Store, Load, RegWrite, ALUop}));

  // Notes on the sheet:
  //   contents of rom_1 (hex, n*v repeats v):
  //   c 10 44 64 4 5 6 7
endmodule

module VectorULA (
  input  [7:0] A,
  input  [7:0] B,
  input  [1:0] OP,
  output [7:0] D
);

  wire [7:0] adder_1_out, and_1_out, or_1_out, subtractor_1_out;

  Adder adder_1 (.a(A), .b(B), .out(adder_1_out));  // open: cin, cout
  Subtractor subtractor_1 (.a(A), .b(B), .out(subtractor_1_out));  // open: bin, bout
  assign and_1_out = A & B;  // AND_Gate and_1, 8 bits wide
  assign or_1_out = A | B;  // OR_Gate or_1, 8 bits wide
  Multiplexer #(.select(2), .width(8)) multiplexer_1 (
    .in0(adder_1_out), .in1(subtractor_1_out), .in2(and_1_out), .in3(or_1_out), .out(D), .sel(OP));
endmodule

module IsZero (
  input  [7:0] A,
  output Z
);

  nor nor_1 (Z, A[0], A[1], A[2], A[3], A[4], A[5], A[6], A[7]);
endmodule
